# Fritzing sketch waterFlow (saved by Fritzing 0.9.3b)
breadboards: 1

parts:
  YF-S201_Flow_Meter = YF-S201 Water Flow Meter
  NodeMCU = NodeMCU V1.0
  9v_For_NodeMCU = Battery block 9V
  LED = smd LED [color="Red (633nm)" package="1206 [SMD]"]
  12v_Solenoid_Valve = Plastic Solenoid Valve
  Realy_Module = Keyes Relay [package=THT]
  12v_Battery_For_Valve = 4 x AAA Battery Mount

nets:
  N1: YF-S201_Flow_Meter.SIG, NodeMCU.D2
  GND: YF-S201_Flow_Meter.GND, NodeMCU.GND, 9v_For_NodeMCU.-, LED.cathode, Realy_Module.ground
  VCC: YF-S201_Flow_Meter.VCC, NodeMCU.3V3
  N2: NodeMCU.D1, LED.anode, Realy_Module.signal
  N3: NodeMCU.Vin, 9v_For_NodeMCU.+, Realy_Module.power
  N4: 12v_Solenoid_Valve.no_name_yet#1, 12v_Battery_For_Valve.+
  N5: 12v_Solenoid_Valve.no_name_yet#2, Realy_Module.NO
  N6: Realy_Module.C, 12v_Battery_For_Valve.-

custom parts:
  YF-S201 Water Flow Meter: The YF-S201 Flow Meter. The input voltage is 5V to 24V (DC).
  NodeMCU V1.0: ESP8266 based NodeMCU
  Keyes Relay: The Keyes 5V relay module is suitable for SCM development, home appliance control. It uses a 5V~12V TIL control signal which can control DC / AC signal.
